# Fritzing sketch puck-v1 (saved by Fritzing 0.9.3b)
perfboards: 1

parts:
  Part3 = Adafruit ItsyBitsy M4 [part_number="Adafruit #3800"]
  Lipo_In = Header 2 [package=jst-2-smd]
  DOTSTAR3 = DotStar Strip -- Black (60/m) [part_number=2239]
  J1 = Piezo Speaker
  S1 = Toggle Switch [package=THT]
  Trigger = SWITCH-MOMENTARY-2 [package=tactile-pth-12mm]
  IR5 = TSOP312.., 314.. [package=THT]
  LED7 = LED - 5mm [color="Infrared (940nm)" package="5 mm [THT]"]
  U8 = TRANSISTOR_NPN_2 [part_number=PN2222 package=to-92]
  R12 = Resistor [tolerance=±5% resistance=470 package="0805 [SMD]"]
  R13 = Trimmer Potentiometer [maximum_resistance=50kΩ package=THT]

nets:
  N1: Part3.EN, S1.L1
  N2: Part3.D4, R12.Pin_0
  N3: Part3.VBAT, Lipo_In.1
  N4: Part3.GND, Lipo_In.2, S1.COM
  N5: Part3.D10, Trigger.1
  N6: Part3.D9, J1.pin2
  N7: Part3.D7, IR5.GND
  N8: Part3.D5_5V, DOTSTAR3.CI
  N9: Part3.VHI, DOTSTAR3.+5V
  N10: LED7.cathode, U8.E
  N11: LED7.anode, R13.wiper
  N12: U8.B, R12.Pin_1

custom parts:
  Adafruit ItsyBitsy M4: What's smaller than a Feather but larger than a Trinket? It's an Adafruit ItsyBitsy M4 Express featuring the Microchip ATSAMD51! Small, powerful, with a ultra fast ATSAMD51 Cortex M4 processor running at 120 MHz - this microcontroller board is perfect when you want something very compact, with a ton of horsepower and a bunch of pins. This Itsy is like a bullet train, with it's 120MHz Cortex M4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
  DotStar Strip -- Black (60/m): NeopixelDotStar Strip, Black, 60 pixels per meter.
