# Fritzing sketch spell-stone-1 (saved by Fritzing 0.9.3b)
perfboards: 1

parts:
  Part1 = Adafruit ItsyBitsy M4 [part_number="Adafruit #3800"]
  S1 = Toggle Switch [package=THT]
  Part2 = Adafruit Switched JST Breakout [part_number="Adafruit #1863"]
  IO_Connector = shrouded pin header, 8 pins [form="♂ (shrouded male)"]
  MCU_Interconnect = shrouded pin header, 10 pins [form="♂ (shrouded male)"]
  U1 = POT [package=alps_pot]
  C1 = Electrolytic Capacitor [capacitance=100μF voltage=16V package="0807 [SMD, electrolytic]"]
  TRS1 = Audio Jack (TRS) 3.5mm [package="4Ucon 08780 [THT]"]
  U2 = TRANSISTOR_NPN_2 [part_number=PN2222 package=to-92]
  LED3 = LED - 5mm [color="Infrared (940nm)" package="5 mm [THT]"]
  R2 = Resistor [tolerance=±5% resistance=470 package="0805 [SMD]"]
  IR2 = TSOP312.., 314.. [package=THT]
  DOTSTAR1 = DotStar Strip -- Black (60/m) [part_number=2239]
  LED4 = prefix0000
  Part3 = Adafruit MicroSD card breakout board [part_number="Adafruit #254"]
  Part4 = Adafruit MMA8451 Accelerometer [part_number="Adafruit #2019"]
  U3 = TRANSISTOR_NPN_2 [part_number=PN2222 package=to-92]  # not connected
  R3 = Resistor [tolerance=±5% resistance=470 package="0805 [SMD]"]  # not connected
  J2 = female pin header, 2 pins [form="♀ (female)"]  # not connected

nets:
  N1: Part1.D3, IR2.GND
  N2: Part1.D4, R2.Pin_1
  N3: Part1.VBAT, S1.COM
  GND: Part1.GND, Part2.GND
  N4: Part1.D12, DOTSTAR1.CI
  N5: Part1.D11, DOTSTAR1.DI
  N6: Part1.D10, LED4.connector2
  N7: Part1.SCL, Part4.SCL
  N8: Part1.SDA, Part4.SDA
  N9: Part1.TX_D1, MCU_Interconnect.pin10
  N10: Part1.RX_D0, MCU_Interconnect.pin1
  N11: Part1.D2, Part3.CS
  N12: Part1.MISO, Part3.DO
  N13: Part1.MOSI, Part3.DI
  N14: Part1.SCK, Part3.CLK
  N15: Part1.A5, IO_Connector.pin3
  N16: Part1.A4, IO_Connector.pin7
  N17: Part1.A3, IO_Connector.pin2
  N18: Part1.A2, IO_Connector.pin8
  N19: Part1.A1, IO_Connector.pin1
  N20: Part1.A0, U1.A
  N21: S1.L1, Part2.V+
  N22: U1.S, C1.-
  N23: C1.+, TRS1.Ring, TRS1.Tip
  N24: U2.B, R2.Pin_0
  N25: U2.E, LED3.cathode

notes:
  Optional audio
  Optional SD for audio, data, etc
  Optional IMU

custom parts:
  Adafruit ItsyBitsy M4: What's smaller than a Feather but larger than a Trinket? It's an Adafruit ItsyBitsy M4 Express featuring the Microchip ATSAMD51! Small, powerful, with a ultra fast ATSAMD51 Cortex M4 processor running at 120 MHz - this microcontroller board is perfect when you want something very compact, with a ton of horsepower and a bunch of pins. This Itsy is like a bullet train, with it's 120MHz Cortex M4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
  Adafruit Switched JST Breakout: This switched JST connector is the best way to quickly prototype with our LiPoly batteries. We paired a genuine JST connector with a slide switch that can do up to 600mA. Both are soldered onto a breadboard-friendly breakout. There's two ground pins, one 'switched' power pin, and one pin that is always on. This is compatible with the "JST PH 2-pin" connectors we use in our battery packs..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
  DotStar Strip -- Black (60/m): NeopixelDotStar Strip, Black, 60 pixels per meter.
  Adafruit MicroSD card breakout board: Not just a simple breakout board, this microSD adapter goes the extra mile - designed for ease of use. Onboard 5v->3v regulator provides 150mA for power-hungry cards 3v level shifting means you can use this with ease on either 3v or 5v systems Uses a proper level shifting chip, not resistors: less problems, and faster read/write access Use 3 or 4 digital pins to read and write 2Gb+ of storage!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
  Adafruit MMA8451 Accelerometer: So many accelerometers and so little time! We've expanded our accelerometer selection even more with this high-precision and inexpensive MMA8451 Triple-Axis Accelerometer w/ 14-bit ADC. You can detect motion, tilt and basic orientation with a digital accelerometer - and the MMA8451 is a great accelerometer to start with. It has a wide usage range, from +-2g up to +-8g yet is easy to use with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
