# Fritzing sketch spell-stone-minimal (saved by Fritzing 0.9.3b)
stripboards: 1

parts:
  Part2 = Adafruit ItsyBitsy M4 [part_number="Adafruit #3800"]
  LED4 = LED - 5mm [color="Infrared (940nm)" package="5 mm [THT]"]
  IR3 = TSOP312.., 314.. [package=THT]
  DOTSTAR2 = DotStar Strip -- Black (60/m) [part_number=2239]
  U4 = TRANSISTOR_NPN_2 [part_number=PN2222 package=to-92]
  R4 = Resistor [tolerance=±5% resistance=470 package="0805 [SMD]"]
  Power_In = Header 2 [package=jst-2-smd]

nets:
  N1: Part2.D3, IR3.GND
  +3V3: Part2.D4, Part2.+3V3, LED4.cathode, LED4.anode, IR3.Data, DOTSTAR2.+5V, U4.B, U4.E, R4.Pin_0, R4.Pin_1
  N2: Part2.VBAT, Power_In.2
  GND: Part2.GND, IR3.Vs, DOTSTAR2.GND, U4.C, Power_In.1
  N3: Part2.D12, DOTSTAR2.CI
  N4: Part2.D11, DOTSTAR2.DI

custom parts:
  Adafruit ItsyBitsy M4: What's smaller than a Feather but larger than a Trinket? It's an Adafruit ItsyBitsy M4 Express featuring the Microchip ATSAMD51! Small, powerful, with a ultra fast ATSAMD51 Cortex M4 processor running at 120 MHz - this microcontroller board is perfect when you want something very compact, with a ton of horsepower and a bunch of pins. This Itsy is like a bullet train, with it's 120MHz Cortex M4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
  DotStar Strip -- Black (60/m): NeopixelDotStar Strip, Black, 60 pixels per meter.
