# Fritzing sketch tool-v2 (saved by Fritzing 0.9.3b)
perfboards: 2

parts:
  Part3 = Adafruit ItsyBitsy M4 [part_number="Adafruit #3800"]
  IR4 = TSOP312.., 314.. [package=THT]
  LED5 = LED - 5mm [color="Infrared (940nm)" package="5 mm [THT]"]
  U5 = TRANSISTOR_NPN_2 [part_number=PN2222 package=to-92]
  R5 = Resistor [tolerance=±5% resistance=470 package="0805 [SMD]"]
  Lipo_In = Header 2 [package=jst-2-smd]
  DOTSTAR3 = DotStar Strip -- Black (60/m) [part_number=2239]
  Part4 = Adafruit LIS3DH [part_number="Adafruit #2809"]
  J1 = Piezo Speaker
  R7 = Trimmer Potentiometer [maximum_resistance=50kΩ package=THT]
  S1 = Toggle Switch [package=THT]
  Trigger = SWITCH-MOMENTARY-2 [package=tactile-pth-12mm]
  U7 = TRANSISTOR_NPN_2 [part_number=PN2222 package=to-92]
  R10 = Resistor [tolerance=±5% resistance=470 package="0805 [SMD]"]
  R11 = Trimmer Potentiometer [maximum_resistance=50kΩ package=THT]
  LED6 = LED - 5mm [color="Infrared (940nm)" package="5 mm [THT]"]
  U8 = TRANSISTOR_NPN_2 [part_number=PN2222 package=to-92]
  R12 = Resistor [tolerance=±5% resistance=470 package="0805 [SMD]"]
  R13 = Trimmer Potentiometer [maximum_resistance=50kΩ package=THT]
  LED7 = LED - 5mm [color="Infrared (940nm)" package="5 mm [THT]"]

nets:
  N1: Part3.D4, R5.Pin_0
  N2: Part3.VBAT, S1.COM
  GND: Part3.GND, IR4.Vs, U5.C, Lipo_In.2, DOTSTAR3.GND, Part4.GND, J1.pin1, Trigger.2
  N3: Part3.D9, J1.pin2
  N4: Part3.D7, IR4.GND
  N5: Part3.D5_5V, DOTSTAR3.CI
  N6: Part3.SCL, Part4.SCL
  N7: Part3.SDA, Part4.SDA
  N8: Part3.A5, Trigger.1
  N9: Part3.VHI, DOTSTAR3.+5V
  +3V3: Part3.+3V3, IR4.Data, Part4.VIN, R7.leg1
  N10: LED5.cathode, U5.E
  N11: LED5.anode, R7.wiper
  N12: U5.B, R5.Pin_1
  N13: Lipo_In.1, S1.L1
  N14: U7.B, R10.Pin_1
  N15: U7.E, LED6.cathode
  N16: R11.leg1, LED6.anode
  N17: U8.B, R12.Pin_1
  N18: U8.E, LED7.cathode
  N19: R13.wiper, LED7.anode

custom parts:
  Adafruit ItsyBitsy M4: What's smaller than a Feather but larger than a Trinket? It's an Adafruit ItsyBitsy M4 Express featuring the Microchip ATSAMD51! Small, powerful, with a ultra fast ATSAMD51 Cortex M4 processor running at 120 MHz - this microcontroller board is perfect when you want something very compact, with a ton of horsepower and a bunch of pins. This Itsy is like a bullet train, with it's 120MHz Cortex M4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
  DotStar Strip -- Black (60/m): NeopixelDotStar Strip, Black, 60 pixels per meter.
  Adafruit LIS3DH: The LIS3DH is a very popular low power triple-axis accelerometer. It's low-cost, but has just about every 'extra' you'd want in an accelerometer: Three axis sensing, 10-bit precision ±2g/±4g/±8g/±16g selectable scaling Both I2C (2 possible addresses) and SPI interface options Interrupt output Multiple data rate options 1 Hz to 5Khz As low as 2uA current draw (just the chip itself, not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
